# Fritzing sketch H (saved by Fritzing 0.9.2b)
breadboards: 1

parts:
  Q4 = BD140 [package="TO220 [THT]"]
  Q5 = BD139 [package="TO220 [THT]"]
  Q6 = BD140 [package="TO220 [THT]"]
  Q7 = BD139 [package="TO220 [THT]"]
  Q1 = NPN-Transistor [package="TO92 [THT]"]
  R1 = Resistor [tolerance=±5% resistance=1k package=THT]
  R2 = Resistor [tolerance=±5% resistance=1k package=THT]
  Q8 = NPN-Transistor [package="TO92 [THT]"]
  R3 = Resistor [tolerance=±5% resistance=10k package=THT]
  R4 = Resistor [tolerance=±5% resistance=10k package=THT]

nets:
  N1: Q4.emitter, Q6.emitter
  N2: Q4.collector, Q5.collector
  N3: Q4.base, R1.Pin_0
  N4: Q5.emitter, Q7.emitter
  N5: Q5.base, Q8.E
  N6: Q6.collector, Q7.collector
  N7: Q6.base, R2.Pin_0
  N8: Q7.base, Q1.E
  N9: Q1.B, R4.Pin_1
  N10: Q1.C, R1.Pin_1
  N11: R2.Pin_1, Q8.C
  N12: Q8.B, R3.Pin_1

custom parts:
  BD140: A pnp transistor which can drive a higher load
  BD139: A npn transistor which can drive a higher load
