# Fritzing sketch amplifier (saved by Fritzing 0.9.2b)
breadboards: 1

parts:
  Part1 = Arduino Uno (Rev3)
  R1 = Resistor [tolerance=±5% resistance=220 package=THT]
  R2 = Resistor [tolerance=±5% resistance=220 package=THT]
  C1 = Ceramic Capacitor [capacitance=100nF package="100 mil [THT, multilayer]"]
  MIC1 = Microphone

nets:
  N1: Part1.A0, R1.Pin_1, R2.Pin_0, C1.1
  N2: R2.Pin_1, MIC1.pin1
  N3: C1.0, MIC1.pin2
