# Fritzing sketch voltreg (saved by Fritzing 0.9.2b)
breadboards: 1

parts:
  U1 = Voltage Regulator [package=to220-adj]
  R1 = Resistor [tolerance=±5% resistance=1k package=THT]
  R2 = Rotary Potentiometer (Large) [maximum_resistance=100kΩ package=THT]

nets:
  N1: U1.ADJ, R1.Pin_0, R2.leg1
  N2: U1.OUT, R1.Pin_1

notes:
  Input = +12V (rood)
  Gnd = blauw
  Output (paars)
